# Fritzing sketch PoolMonitor (saved by Fritzing 0.9.2b)

parts:
  Part1 = Arduino Uno (Rev3)
  TFT1 = 2.2" TFT with MicroSD Breakout [part_number="ST7735 1.8 TFT LCD"]
  DS1 = DS18B20 1-Wire Temperature Sensor Probe Cable [part_number="DS18B20 https://www.sparkfun.com/products/11050"]
  R1 = Resistor [tolerance=±5% resistance=4.7k package="0402 [SMD]"]

nets:
  N1: Part1.D8, TFT1.SDCS
  N2: Part1.D9_PWM, TFT1.CS
  N3: Part1.D10_PWM/SS, TFT1.RST
  N4: Part1.D11_PWM/MOSI, TFT1.MOSI
  N5: Part1.D13/SCK, TFT1.SCK
  N6: Part1.D2, DS1.DQ, R1.Pin_0
  N7: Part1.3V3, TFT1.BL
  N8: Part1.GND, TFT1.MISO
  N9: DS1.VDD, R1.Pin_1

notes:
  SAINSMART TFT LCD breakout
  vcc - gnd - scl - sda - ps/dc - res - cs
  3v - gnd - 13 - 11 - 9 - 8 - 10
  Temperature Sensor -Waterproof (DS1820)

custom parts:
  2.2" TFT with MicroSD Breakout: 2.2" TFT Display with HX8340B Controller and MicroSD Card
